# Fritzing sketch battery_indicator (saved by Fritzing 0.8.7b)
breadboards: 1

parts:
  Part1 = Arduino Uno (Rev3)
  LED2 = LED - 5mm [color="Red (633nm)" package="5 mm [THT]"]
  LED4 = LED - 5mm [color="Green (560nm)" package="5 mm [THT]"]
  LED6 = LED - 5mm [color="Yellow (585nm)" package="5 mm [THT]"]
  Resistor3 = Resistor [tolerance=±5% resistance=220 package=THT]
  Resistor5 = Resistor [tolerance=±5% resistance=220 package=THT]
  Resistor1 = Resistor [tolerance=±5% resistance=220 package=THT]

nets:
  N1: Part1.A0, Resistor1.Pin_0
  N2: Part1.A1, Resistor5.Pin_0
  N3: Part1.A2, Resistor3.Pin_0
  N4: Part1.GND, LED2.cathode, LED4.cathode, LED6.cathode
  N5: LED2.anode, Resistor1.Pin_1
  N6: LED4.anode, Resistor3.Pin_1
  N7: LED6.anode, Resistor5.Pin_1

notes:
  We will be cutting the "SNS1 & SNS0" on the motor shield to free up pins A0 & A1.
