# Fritzing sketch light_detector (saved by Fritzing 0.8.7b)
breadboards: 1

parts:
  Part1 = Arduino Uno (Rev3)
  T1 = LM35 Temperature Sensor [package="TO92 [THT]"]

nets:
  N1: Part1.A0, T1.Vout
  GND: Part1.GND, T1.GND
  N2: Part1.5V, T1.+Vs

notes:
  https://learn.adafruit.com/tmp36-temperature-sensor
